# Fritzing sketch AtariPunkConsole_556 (saved by Fritzing 0.9.10b)
breadboards: 1

parts:
  U1 = 556 [package=dil14]
  R1 = Resistor [tolerance=±5% power=0.25 resistance=1k package=THT]
  VCC1 = Battery block 9V
  R2 = Rotary Potentiometer (Small) [maximum_resistance=500kΩ knob_status=50% power=0.5W package=THT]
  R3 = Rotary Potentiometer (Small) [maximum_resistance=500kΩ knob_status=50% power=0.5W package=THT]
  C1 = Ceramic Capacitor [capacitance=100nF voltage=35V package="100 mil [THT, multilayer]"]
  C2 = Ceramic Capacitor [capacitance=100nF voltage=35V package="100 mil [THT, multilayer]"]
  S1 = Toggle Switch [package=THT]
  J1 = Piezo Speaker
  R4 = Rotary Potentiometer (Small) [maximum_resistance=100kΩ knob_status=50% power=0.5W package=THT]

nets:
  N1: U1.DIS, R1.Pin_0, R3.leg1
  N2: U1.THR, U1.TRIG, R1.Pin_1, C1.1
  N3: U1.RST, U1.RST2, U1.VCC, VCC1.+, R2.wiper, R3.wiper, J1.pin2
  N4: U1.OUT, U1.TRIG2
  N5: U1.GND, VCC1.-, C1.0, C2.0
  N6: U1.OUT2, S1.COM
  N7: U1.THR2, U1.DIS2, R2.leg1, C2.1
  N8: S1.L2, R4.leg1
