# Fritzing sketch AtariPunkConsole_556_bb (saved by Fritzing 0.9.10b)
breadboards: 1

parts:
  U1 = 556 [package=dil14]
  R1 = Resistor [tolerance=±5% power=0.25 resistance=1k package=THT]
  C2 = Ceramic Capacitor [capacitance=100nF voltage=35V package="100 mil [THT, multilayer]"]
  Piezo = Piezo Speaker - PC Mount [part_number=COM-07950]
  R1_2 = Big Potentiometer [part_number=50K]
  R2 = Big Potentiometer [part_number=50K]
  C1 = Ceramic Capacitor [capacitance=100nF voltage=35V package="100 mil [THT, multilayer]"]
  VCC2 = Battery block 9V
  R3 = Big Potentiometer [part_number=5K]

nets:
  N1: U1.DIS, R1.Pin_0
  N2: U1.THR, U1.TRIG, R1.Pin_1, R1_2.leg1, C1.1
  VCC: U1.RST, U1.RST2, U1.VCC, Piezo.VCC, R1_2.wiper, R2.leg1, VCC2.+
  N3: U1.OUT, U1.TRIG2
  N4: U1.GND, C2.0, C1.0, VCC2.-
  N5: U1.OUT2, R3.wiper
  N6: U1.THR2, U1.DIS2, C2.1, R2.wiper
  N7: Piezo.GND, R3.leg1

custom parts:
  Piezo Speaker - PC Mount: This is a small 12mm round speaker that operates around the audible 2kHz range. You can use these speakers to create simple music or user interfaces. Each speaker is PTH solderable and requires an operating voltage of 3.5-5V with a mean current of 35mA max. These speakers also have a typical sound output of 95 dBA and a coil resistance of 42 ±6.3 ohms.
  Big Potentiometer: A standard adjustable resistor (potentiometer).
