# Fritzing sketch 4017_1 (saved by Fritzing 0.9.10b)
breadboards: 1

parts:
  U1 = 4017 [chip_label=4017 package="DIP (Dual Inline) [THT]"]
  U2 = 7-SEGMENT-DISPLAY [package=7-segment-display]  # not connected
  U3 = 555 Timer [package="DIP8 [THT]"]
  VCC1 = Battery block 9V
  C1 = Electrolytic Capacitor [capacitance=4.7µF voltage=35V package="100 mil [THT, electrolytic]"]
  R1 = Resistor [tolerance=±5% resistance=10k package="1206 [SMD]"]
  R2 = Resistor [tolerance=±5% resistance=10k package="1206 [SMD]"]

nets:
  N1: U1.pin8, U1.pin13, U1.pin15, U3.Ground, VCC1.-, C1.-
  N2: U1.pin14, U3.Output
  N3: U1.pin16, U3.Reset, U3.Vcc_Supply_Voltage, VCC1.+, R1.Pin_0
  N4: U3.Trigger, U3.Threshold, C1.+, R2.Pin_1
  N5: U3.Discharge, R1.Pin_1, R2.Pin_0

custom parts:
  4017: 4017 CMOS decade counter with 10 decoded outputs
