# Fritzing sketch voltageLadder (saved by Fritzing 0.9.6b)
breadboards: 1

parts:
  S1 = Pushbutton [package="[THT]"]
  S2 = Pushbutton [package="[THT]"]
  S3 = Pushbutton [package="[THT]"]
  S4 = Pushbutton [package="[THT]"]
  R1 = Resistor [tolerance=±5% power=0.25 resistance=2k package=THT]
  Part1 = Arduino Uno (Rev3) - ICSP
  R2 = Resistor [tolerance=±5% power=0.25 resistance=330 package=THT]
  R3 = Resistor [tolerance=±5% power=0.25 resistance=680 package=THT]
  R4 = Resistor [tolerance=±5% power=0.25 resistance=1k package=THT]
  R5 = Resistor [tolerance=±5% power=0.25 resistance=3.3k package=THT]
  S5 = Pushbutton [package="[THT]"]

nets:
  N1: S1.Pin_1, S1.Pin_2, S2.Pin_1, S2.Pin_2, S3.Pin_1, S3.Pin_2, S4.Pin_1, S4.Pin_2, Part1.GND, S5.Pin_1, S5.Pin_2
  N2: S1.Pin_3, S1.Pin_4, R1.Pin_1, Part1.A0, R2.Pin_0
  N3: S2.Pin_3, S2.Pin_4, R2.Pin_1, R3.Pin_0
  N4: S3.Pin_3, S3.Pin_4, R3.Pin_1, R4.Pin_0
  N5: S4.Pin_3, S4.Pin_4, R4.Pin_1, R5.Pin_0
  N6: R1.Pin_0, Part1.5V
  N7: R5.Pin_1, S5.Pin_3, S5.Pin_4
