# Fritzing sketch BristleBot (saved by Fritzing 0.9.6b)
breadboards: 2

parts:
  M1 = DC Motor
  BAT1 = Battery Holders [package=battcom_20mm_pth]

nets:
  N1: M1.pin_1, BAT1.-
  N2: M1.pin_2, BAT1.+
