# Fritzing sketch LED Short Circuit - Week 2 Homework (saved by Fritzing 0.9.6b)
circuit board: 6.9215cm x 5.33756cm
breadboards: 1

parts:
  COIN_CELL = Battery Holders [package=battcom_20mm_pth]
  MOMENTARY_PUSH_BUTTON = Momentary Switch [package=ksa_sealed_tac_switch]
  RED_LED = smd LED [color="Red (635nm)" package="0805 [SMD]"]
  WHITE_LED = smd LED [color="White (6500K)" package="0805 [SMD]"]

nets:
  N1: COIN_CELL.+, RED_LED.cathode, WHITE_LED.cathode
  N2: COIN_CELL.-, MOMENTARY_PUSH_BUTTON.4, WHITE_LED.anode
  N3: MOMENTARY_PUSH_BUTTON.2, RED_LED.anode
