# Fritzing sketch simpleDC-powerSupply (saved by Fritzing 0.9.4)
breadboards: 1

parts:
  DC_Motor = DC Motor
  Power_Supply = Breadboard Power Supply Board SMD

nets:
  N1: DC_Motor.pin_1, Power_Supply.VCC
  N2: DC_Motor.pin_2, Power_Supply.GND
