# Fritzing sketch AtariPunkConsole_2x555 (saved by Fritzing 0.9.9b)
breadboards: 1

parts:
  U2 = 555 Timer [package="DIP8 [THT]"]
  U1 = 555 Timer [package="DIP8 [THT]"]
  C1 = Capacitor [part_number="0.01 uF" package=cap-pth-small2]
  C2 = Capacitor [part_number="0.01 uF" package=cap-pth-small2]
  C3 = Electrolytic Capacitor [capacitance=10µF voltage=35V package="100 mil [THT, electrolytic]"]
  U3 = POT [part_number=500k package=alps_pot]
  R1 = Resistor [tolerance=±5% resistance=220 package="0805 [SMD]"]
  U4 = POT [part_number=500k package=alps_pot]
  VCC1 = Battery block 9V
  SP1 = SPEAKER [package=pcb_mount_speaker]

nets:
  N1: U2.Ground, U1.Ground, C1.1, C2.1, U3.E, U4.A, VCC1.-
  N2: U2.Trigger, U1.Output
  N3: U2.Output, C3.-
  N4: U2.Reset, U2.Vcc_Supply_Voltage, U1.Reset, U1.Vcc_Supply_Voltage, U3.S, U4.S, VCC1.+, SP1.-
  N5: U2.Control_Voltage, U3.A
  N6: U2.Threshold, U2.Discharge, C2.2
  N7: U1.Trigger, U1.Threshold, C1.2, R1.Pin_1
  N8: U1.Discharge, R1.Pin_0, U4.E
  N9: C3.+, SP1.+
