# Fritzing sketch AtariPunkConsole_556-dual output (saved by Fritzing 0.9.10b)
breadboards: 1

parts:
  U1 = 556 [package=dil14]
  R1 = Resistor [tolerance=±5% power=0.25 resistance=1k package=THT]
  VCC1 = Battery block 9V
  R2 = Rotary Potentiometer (Small) [maximum_resistance=500kΩ knob_status=50% power=0.5W package=THT]
  R3 = Rotary Potentiometer (Small) [maximum_resistance=500kΩ knob_status=50% power=0.5W package=THT]
  C1 = Ceramic Capacitor [capacitance=0.01µF voltage=35V part_number=100nF package="100 mil [THT, multilayer]"]
  C2 = Ceramic Capacitor [capacitance=0.01µF voltage=35V part_number=100nF package="100 mil [THT, multilayer]"]
  Output_Selector_Switch = Toggle Switch [package=THT]
  Piezo_Buzzer = Piezo Speaker
  R4 = Rotary Potentiometer (Small) [maximum_resistance=5kΩ knob_status=50% power=0.5W part_number=Volume package=THT]
  R6 = Resistor [tolerance=±5% power=0.25 resistance=10k package=THT]
  C3 = Ceramic Capacitor [capacitance=10µF voltage=35V package="100 mil [THT, multilayer]"]
  R7 = Resistor [tolerance=±5% power=0.25 resistance=4.7k package=THT]
  Mini_Jack_(mono_summed) = Audio Jack (TRS) 3.5mm [package="PG203J [THT]"]

nets:
  N1: U1.DIS, R1.Pin_0, R3.leg1
  N2: U1.THR, U1.TRIG, R1.Pin_1, C1.1
  N3: U1.RST, U1.RST2, U1.VCC, VCC1.+, R2.wiper, R3.wiper, Piezo_Buzzer.pin2
  N4: U1.OUT, U1.TRIG2
  N5: U1.GND, VCC1.-, C1.0, C2.0, R7.Pin_0, Mini_Jack_(mono_summed).Sleeve
  N6: U1.OUT2, Output_Selector_Switch.COM
  N7: U1.THR2, U1.DIS2, R2.leg1, C2.1
  N8: Output_Selector_Switch.L1, C3.0
  N9: Output_Selector_Switch.L2, R4.leg1
  N10: Piezo_Buzzer.pin1, R4.wiper
  N11: R6.Pin_0, R7.Pin_1, Mini_Jack_(mono_summed).Ring, Mini_Jack_(mono_summed).Tip
  N12: R6.Pin_1, C3.1
