# Fritzing sketch BasicLEDPlayground (saved by Fritzing 0.9.10b)
breadboards: 1

parts:
  Part1 = Arduino Uno (Rev3)
  RGB_LED = RGB LED - (4 legs) [package="5 mm [THT]"]
  Yellow_LED = LED - 5mm [color="Yellow (574nm)" current=0.030 package="5 mm [THT]"]
  White_LED = LED - 5mm [color="White (6500K)" current=0.030 package="5 mm [THT]"]
  Red_LED = LED - 5mm [color="Red (635nm)" current=0.030 package="5 mm [THT]"]
  Green_LED = LED - 5mm [color="Green (560nm)" current=0.030 package="5 mm [THT]"]
  Blue_LED = LED - 5mm [color="Blue (430nm)" current=0.030 package="5 mm [THT]"]
  R1 = Resistor [tolerance=±5% resistance=330 package="2010 [SMD]"]
  R2 = Resistor [tolerance=±5% resistance=330 package="2010 [SMD]"]
  R3 = Resistor [tolerance=±5% resistance=330 package="2010 [SMD]"]
  R4 = Resistor [tolerance=±5% resistance=330 package="2010 [SMD]"]
  R5 = Resistor [tolerance=±5% resistance=330 package="2010 [SMD]"]
  R6 = Resistor [tolerance=±5% resistance=330 package="2010 [SMD]"]
  R7 = Resistor [tolerance=±5% resistance=330 package="2010 [SMD]"]
  R8 = Resistor [tolerance=±5% resistance=330 package="2010 [SMD]"]

nets:
  N1: Part1.D9_PWM, R5.Pin_0
  N2: Part1.D10_PWM/SS, R4.Pin_0
  N3: Part1.D11_PWM/MOSI, R3.Pin_0
  N4: Part1.D12/MISO, R1.Pin_0
  N5: Part1.D13/SCK, R2.Pin_0
  N6: Part1.D3_PWM, R8.Pin_0
  N7: Part1.D5_PWM, R7.Pin_0
  N8: Part1.D6_PWM, R6.Pin_0
  N9: Part1.GND, RGB_LED.common_anode, Yellow_LED.cathode, White_LED.cathode, Red_LED.cathode, Green_LED.cathode, Blue_LED.cathode
  N10: RGB_LED.red_cathode, R6.Pin_1
  N11: RGB_LED.green_cathode, R7.Pin_1
  N12: RGB_LED.blue_cathode, R8.Pin_1
  N13: Yellow_LED.anode, R1.Pin_1
  N14: White_LED.anode, R2.Pin_1
  N15: Red_LED.anode, R3.Pin_1
  N16: Green_LED.anode, R4.Pin_1
  N17: Blue_LED.anode, R5.Pin_1
