# Fritzing sketch WS2812_BreadboardPoweredArduino (saved by Fritzing 0.9.6b)
breadboards: 1

parts:
  Part1 = Arduino Uno (Rev3)
  YwRobot_Power_Supply1 = YwRobot Breadboard Power Supply [part_number=545043]  # not connected
  U1 = WS2812 RGB LED strip

nets:
  N1: Part1.D13/SCK, U1.DIN
  5V: Part1.5V, U1.VCC
  GND: Part1.GND, U1.GND

custom parts:
  YwRobot Breadboard Power Supply: The YwRobot Breadboard Power Supply (MB-V2) has two power rails; they can be 5V or 3V3. Power to the module can be provided through the female USB socket or through the A10 (female) 2.1mm power jack.
  WS2812 RGB LED strip: WS2812 strip
