# Fritzing sketch WS2812_StraightToArduino (saved by Fritzing 0.9.6b)

parts:
  Part1 = Arduino Uno (Rev3)
  U1 = WS2812 RGB LED strip

nets:
  N1: Part1.D13/SCK, U1.DIN
  5V: Part1.5V, U1.VCC
  GND: Part1.GND, U1.GND

custom parts:
  WS2812 RGB LED strip: WS2812 strip
