# Fritzing sketch ColourMixerV1 (saved by Fritzing 0.9.6b)
breadboards: 1

parts:
  Part1 = Arduino Uno (Rev3) - ICSP
  LCD1 = LCD screen
  R1 = Trimmer Potentiometer [maximum_resistance=10kΩ package=THT]
  LED1 = RGB LED (com. cathode, rgb) [package="5 mm [THT]"]
  R2 = Resistor [tolerance=±5% power=0.25 resistance=220 package=THT]
  Rotary_Encoder = KY-040 Rotary encoder [package="Breakout board"]

nets:
  N1: Part1.ICSP_MISO, Part1.D12/MISO, LCD1.E
  N2: Part1.ICSP_SCK, Part1.D13/SCK, LCD1.RS
  N3: Part1.ICSP_MOSI, Part1.D11_PWM/MOSI, LCD1.DB4
  GND: Part1.GND, LCD1.VSS, LCD1.R/W, LCD1.LED-, R1.leg2, LED1.common_cathode, Rotary_Encoder.GND
  5V: Part1.5V, LCD1.VDD, R1.leg1, R2.Pin_1, Rotary_Encoder.Vcc
  N4: Part1.D8, LCD1.DB5
  N5: Part1.D9_PWM, LED1.green_anode
  N6: Part1.D10_PWM/SS, LED1.red_anode
  N7: Part1.D2, Rotary_Encoder.CLK
  N8: Part1.D3_PWM, Rotary_Encoder.DT
  N9: Part1.D4, Rotary_Encoder.SW
  N10: Part1.D5_PWM, LCD1.DB7
  N11: Part1.D6_PWM, LED1.blue_anode
  N12: Part1.D7, LCD1.DB6
  N13: LCD1.V0, R1.wiper
  N14: LCD1.LED+, R2.Pin_0

custom parts:
  KY-040 Rotary encoder: KY-040 Rotary Encoder with switch on breakout borad from AZ Delivery
